# Fritzing sketch sweepgen (saved by Fritzing 0.9.3b)
breadboards: 1

parts:
  元件1 = Arduino Nano (Rev3.0)
  S1 = Pushbutton [package="[THT]"]

nets:
  N1: 元件1.GND, S1.Pin_3, S1.Pin_4
  N2: 元件1.D5, S1.Pin_1, S1.Pin_2
